# Fritzing sketch Cartão SD (saved by Fritzing 0.9.5d)
breadboards: 1

parts:
  Componente2 = Arduino Mega 2560 (Rev3)
  microSD2 = MicroSD Card Module

nets:
  5V: Componente2.5V, microSD2.VCC
  GND: Componente2.GND, microSD2.GND
  N1: Componente2.D50, microSD2.MISO
  N2: Componente2.D51, microSD2.MOSI
  N3: Componente2.D52, microSD2.SCK
  N4: Componente2.D53, microSD2.CS
