# Fritzing sketch DHT22 (saved by Fritzing 0.9.5d)
breadboards: 1

parts:
  Componente2 = Arduino Mega 2560 (Rev3)
  DHT2 = DHT22 Humidity and Temperature Sensor

nets:
  N1: Componente2.D8_PWM, DHT2.DATA
  5V: Componente2.5V, DHT2.VDD
  GND: Componente2.GND, DHT2.GND
