# Fritzing sketch Display LCD (saved by Fritzing 0.9.5d)
breadboards: 1

parts:
  Componente2 = Arduino Mega 2560 (Rev3)
  LCD2 = LCD screen
  R6 = TRIMPOT [package=3386u]

nets:
  5V: Componente2.5V, LCD2.VDD, R6.CW
  GND: Componente2.GND, LCD2.VSS, LCD2.R/W, LCD2.LED-, R6.CCW
  N1: Componente2.D22, LCD2.RS
  N2: Componente2.D23, LCD2.E
  N3: Componente2.D24, LCD2.DB3, LCD2.DB4
  N4: Componente2.D25, LCD2.DB5
  N5: Componente2.D26, LCD2.DB6
  N6: Componente2.D27, LCD2.DB7
