# Fritzing sketch Endoder KY-040 (saved by Fritzing 0.9.5d)
breadboards: 1

parts:
  Componente2 = Arduino Mega 2560 (Rev3)
  RE2 = KY-040 Rotary encoder [package=THT]

nets:
  N1: Componente2.D19/RX1, RE2.DT
  N2: Componente2.D18/TX1, RE2.CLK
  5V: Componente2.5V, RE2.Vcc
  GND: Componente2.GND, RE2.GND
  N3: Componente2.D2_PWM, RE2.SW

custom parts:
  KY-040 Rotary encoder: KY-040 Rotary Encoder with switch on breakout borad from AZ Delivery
