# Fritzing sketch RTC DS3231 (saved by Fritzing 0.9.5d)
breadboards: 1

parts:
  Componente2 = Arduino Mega 2560 (Rev3)
  ZS-042_RTC2 = ZS-042 RTC Module

nets:
  N1: Componente2.D21/SCL, ZS-042_RTC2.SCL
  N2: Componente2.D20/SDA, ZS-042_RTC2.SDA
  5V: Componente2.5V, ZS-042_RTC2.VCC
  GND: Componente2.GND, ZS-042_RTC2.GND
