# Fritzing sketch Sensor UV - ML8511 (saved by Fritzing 0.9.5d)
breadboards: 1

parts:
  Componente2 = Arduino Mega 2560 (Rev3)
  Part3 = ML8511 Breakout Board

nets:
  N1: Componente2.A0, Part3.OUT
  3V3: Componente2.A1, Componente2.3V3, Part3.3V3, Part3.EN
  GND: Componente2.GND, Part3.GND

custom parts:
  ML8511 Breakout Board: This breakout board uses the ML8511 UV (ultraviolet) light sensor. The ML8511 works best with light in the 280-390nm wavelengths. The board operates at 2.7 to 3.6V.
