# Fritzing sketch DS18B20 (saved by Fritzing 0.9.5d)
breadboards: 1

parts:
  Componente2 = Arduino Mega 2560 (Rev3)
  R1 = Resistor [tolerance=±5% resistance=4.7k package=THT]
  DS3 = DS18B20 adaptado
  DS4 = DS18B20 adaptado
  R2 = Resistor [tolerance=±5% resistance=4.7k package=THT]

nets:
  VDD: Componente2.5V, R1.Pin_1, DS3.VDD, DS4.VDD, R2.Pin_1
  GND: Componente2.GND, DS3.GND, DS4.GND
  N1: Componente2.D6_PWM, DS3.DQ, R2.Pin_0
  N2: Componente2.D7_PWM, R1.Pin_0, DS4.DQ
